# Fritzing sketch Circuit_1 (saved by Fritzing 0.9.3b)
breadboards: 1

parts:
  元件1 = Arduino Uno (Rev3)  # not connected
  Arduino_CNC_Shield_V3_00_1 = Arduino_CNC_V3.00
  M3 = Stepper Motor - Bipolar
  S2 = Toggle Switch [package=THT]
  S3 = Toggle Switch [package=THT]
  M4 = Stepper Motor - Bipolar
  M2 = Stepper Motor - Bipolar
  M5 = DC Motor
  Power_plug1 = Power plug
  S4 = Toggle Switch [package=THT]
  元件2 = Thumb Joystick

nets:
  N1: Arduino_CNC_Shield_V3_00_1.POWER_-, M5.pin_2, Power_plug1.GND
  N2: Arduino_CNC_Shield_V3_00_1.POWER_+, M5.pin_1, Power_plug1.VCC
  N3: Arduino_CNC_Shield_V3_00_1.X-MTR_'1', M4.A
  N4: Arduino_CNC_Shield_V3_00_1.X-MTR_'2', M4.C
  N5: Arduino_CNC_Shield_V3_00_1.X-MTR_'3', M4.B
  N6: Arduino_CNC_Shield_V3_00_1.X-MTR_'4', M4.D
  N7: Arduino_CNC_Shield_V3_00_1.Z-MTR_'1', M3.A
  N8: Arduino_CNC_Shield_V3_00_1.Z-MTR_'2', M3.C
  N9: Arduino_CNC_Shield_V3_00_1.Z-MTR_'3', M3.B
  N10: Arduino_CNC_Shield_V3_00_1.Z-MTR_'4', M3.D
  N11: Arduino_CNC_Shield_V3_00_1.Y-MTR_'1', M2.A
  N12: Arduino_CNC_Shield_V3_00_1.Y-MTR_'2', M2.C
  N13: Arduino_CNC_Shield_V3_00_1.Y-MTR_'3', M2.B
  N14: Arduino_CNC_Shield_V3_00_1.Y-MTR_'4', M2.D
  5V: Arduino_CNC_Shield_V3_00_1.5V, 元件2.VCC
  GND: Arduino_CNC_Shield_V3_00_1.GND, 元件2.GND
  N15: Arduino_CNC_Shield_V3_00_1.End_Stops_Z-_(and_Z+)_/_SpnEn, S3.COM
  N16: Arduino_CNC_Shield_V3_00_1.End_Stops_Z-_(Gnd), S3.L2
  N17: Arduino_CNC_Shield_V3_00_1.End_Stops_Y-_(and_Y+), S2.COM
  N18: Arduino_CNC_Shield_V3_00_1.End_Stops_Y-_(Gnd), S2.L2
  N19: Arduino_CNC_Shield_V3_00_1.End_Stops_X-_(and_X+), S4.COM
  N20: Arduino_CNC_Shield_V3_00_1.End_Stops_X-_(Gnd), S4.L2
  N21: Arduino_CNC_Shield_V3_00_1.Abort_(Gnd), 元件2.VERT
  N22: Arduino_CNC_Shield_V3_00_1.Hold, 元件2.HORZ

custom parts:
  Arduino_CNC_V3.00: Protoneer Arduino CNC Shield V3.00 If using Grbl V0.9: The “A” axis can not be used (yet). The “SCL” (Arduino A5) pin is now used for 'Probing' input. The “End Stops Z+ & Z-” (Arduino D11) and “SpnEn” (Arduino D12) have been switched!
