# Fritzing sketch Circuit_2 (saved by Fritzing 0.9.3b)
breadboards: 1

parts:
  R = Resistor [tolerance=±5% resistance=101 package=THT]
  C = Ceramic Capacitor [capacitance=100nF package="200 mil [THT, multilayer]"]
  Motor = DC Motor
  VC = 4 x AAA Battery Mount [part_number=4.5V]
  Switch = SWITCH-MOMENTARY-2 [package=tactile_switch_smd-2]

nets:
  N1: R.Pin_0, Motor.pin_1, VC.+
  N2: R.Pin_1, C.0
  N3: C.1, Motor.pin_2, Switch.1
  N4: VC.-, Switch.2
